# Fritzing sketch tmon (saved by Fritzing 0.9.1b)

parts:
  R12 = Resistor [tolerance=±5% resistance=10k package=THT]
  R2 = Resistor [tolerance=±5% resistance=220 package=THT]
  R8 = Resistor [tolerance=±5% resistance=560 package=THT]
  R1 = Resistor [tolerance=±5% resistance=220 package=THT]
  R11 = Resistor [tolerance=±5% resistance=10k package=THT]
  DS1 = DS18B20 1-Wire Temperature Sensor [part_number=DS18B20]
  R13 = Resistor [tolerance=±5% resistance=10k package=THT]
  C4 = Ceramic Capacitor [capacitance=0.1mF package="100 mil [THT, multilayer]"]
  R6 = Resistor [tolerance=±5% resistance=220 package=THT]
  C3 = Ceramic Capacitor [capacitance=0.1mF package="100 mil [THT, multilayer]"]
  C1 = Ceramic Capacitor [capacitance=0.1mF package="100 mil [THT, multilayer]"]
  LED2 = LED - 5mm [color="Green (570nm)" package="5 mm [THT]"]
  R9 = Resistor [tolerance=±5% resistance=10k package=THT]
  C5 = Ceramic Capacitor [capacitance=0.1mF package="100 mil [THT, multilayer]"]
  R10 = Resistor [tolerance=±5% resistance=220 package=THT]
  C2 = Ceramic Capacitor [capacitance=0.1mF package="100 mil [THT, multilayer]"]
  LED1 = LED - 5mm [color="Red (633nm)" package="5 mm [THT]"]
  R14 = Resistor [tolerance=±5% resistance=220 package=THT]
  Raspberry_Pi1 = Raspberry Pi B+
  J4 = female pin header, 2 pins [form="♀ (female)"]
  J5 = female pin header, 2 pins [form="♀ (female)"]
  J6 = female pin header, 2 pins [form="♀ (female)"]
  J7 = female pin header, 2 pins [form="♀ (female)"]
  J8 = female pin header, 2 pins [form="♀ (female)"]
  J9 = female pin header, 3 pins [form="♀ (female)"]
  J10 = female pin header, 3 pins [form="♀ (female)"]
  J11 = female pin header, 3 pins [form="♀ (female)"]
  J12 = female pin header, 3 pins [form="♀ (female)"]
  J13 = female pin header, 16 pins [form="♀ (female)"]

nets:
  N1: R12.Pin_0, C4.1, Raspberry_Pi1.GPIO27
  N2: R12.Pin_1, J5.pin1
  N3: R2.Pin_0, Raspberry_Pi1.GPIO12
  N4: R2.Pin_1, LED2.anode
  5V: R8.Pin_0, Raspberry_Pi1.5V, J13.pin2
  N5: R8.Pin_1, J13.pin15
  N6: R1.Pin_0, Raspberry_Pi1.GPIO25
  N7: R1.Pin_1, LED1.anode
  N8: R11.Pin_0, C3.1, Raspberry_Pi1.GPIO22
  N9: R11.Pin_1, J6.pin1
  3.3V: DS1.VDD, R6.Pin_1, R14.Pin_1, Raspberry_Pi1.3v3, J9.pin3, J10.pin3, J11.pin3, J12.pin3
  N10: DS1.DQ, R6.Pin_0, Raspberry_Pi1.GPIO4, J9.pin2, J10.pin2, J11.pin2, J12.pin2
  GND: DS1.GND, C4.0, C3.0, C1.0, LED2.cathode, C5.0, C2.0, LED1.cathode, Raspberry_Pi1.GND, J9.pin1, J10.pin1, J11.pin1, J12.pin1, J13.pin1, J13.pin3, J13.pin5
  N11: R13.Pin_0, C5.1, Raspberry_Pi1.GPIO17
  N12: R13.Pin_1, J4.pin1
  N13: C1.1, R9.Pin_0, Raspberry_Pi1.GPIO9
  N14: R9.Pin_1, J8.pin1
  N15: R10.Pin_0, C2.1, Raspberry_Pi1.GPIO10
  N16: R10.Pin_1, J7.pin1
  N17: R14.Pin_0, J4.pin2, J5.pin2, J6.pin2, J7.pin2, J8.pin2
  N18: Raspberry_Pi1.GPIO7, J13.pin4
  N19: Raspberry_Pi1.GPIO8, J13.pin6
  N20: Raspberry_Pi1.GPIO23, J13.pin11
  N21: Raspberry_Pi1.GPIO18, J13.pin12
  N22: Raspberry_Pi1.GPIO15, J13.pin13
  N23: Raspberry_Pi1.GPIO14, J13.pin14
